// Logisim project Banco de Registradores OK.circ as structural Verilog: 1 circuit, main circuit main
module main (
  input  Clear,
  input  [7:0] Dado_a_ser_escrito,
  input  Escrever_Reg,
  input  [2:0] Reg_a_ser_escrito,
  input  [2:0] Reg_a_ser_lido_1,
  input  [2:0] Reg_a_ser_lido_2,
  output [7:0] out_7,
  output [7:0] out_8
);

  wire clock_1_out, decoder_1_out0, decoder_1_out1, decoder_1_out2, decoder_1_out3, decoder_1_out4,
       decoder_1_out5, decoder_1_out6, decoder_1_out7;
  wire [7:0] register_1_q, register_2_q, register_3_q, register_4_q, register_5_q, register_6_q,
       register_7_q, register_8_q;

  Decoder #(.select(3)) decoder_1 (
    .out0(decoder_1_out0), .out1(decoder_1_out1), .out2(decoder_1_out2), .out3(decoder_1_out3),
    .out4(decoder_1_out4), .out5(decoder_1_out5), .out6(decoder_1_out6), .out7(decoder_1_out7),
    .sel(Reg_a_ser_escrito), .en(Escrever_Reg));
  Clock clock_1 (.out(clock_1_out));
  Register register_1 (.D(Dado_a_ser_escrito), .en(decoder_1_out0), .Q(register_1_q), .clk(clock_1_out), .clr(Clear));
  Register register_2 (.D(Dado_a_ser_escrito), .en(decoder_1_out1), .Q(register_2_q), .clk(clock_1_out), .clr(Clear));
  Register register_3 (.D(Dado_a_ser_escrito), .en(decoder_1_out2), .Q(register_3_q), .clk(clock_1_out), .clr(Clear));
  Register register_4 (.D(Dado_a_ser_escrito), .en(decoder_1_out3), .Q(register_4_q), .clk(clock_1_out), .clr(Clear));
  Register register_5 (.D(Dado_a_ser_escrito), .en(decoder_1_out4), .Q(register_5_q), .clk(clock_1_out), .clr(Clear));
  Register register_6 (.D(Dado_a_ser_escrito), .en(decoder_1_out5), .Q(register_6_q), .clk(clock_1_out), .clr(Clear));
  Register register_7 (.D(Dado_a_ser_escrito), .en(decoder_1_out6), .Q(register_7_q), .clk(clock_1_out), .clr(Clear));
  Register register_8 (.D(Dado_a_ser_escrito), .en(decoder_1_out7), .Q(register_8_q), .clk(clock_1_out), .clr(Clear));
  Multiplexer #(.select(3), .width(8)) multiplexer_1 (
    .in0(register_1_q), .in1(register_2_q), .in2(register_3_q), .in3(register_4_q), .in4(register_5_q),
    .in5(register_6_q), .in6(register_7_q), .in7(register_8_q), .out(out_7), .sel(Reg_a_ser_lido_1));  // open: en
  Multiplexer #(.select(3), .width(8)) multiplexer_2 (
    .in0(register_1_q), .in1(register_2_q), .in2(register_3_q), .in3(register_4_q), .in4(register_5_q),
    .in5(register_6_q), .in6(register_7_q), .in7(register_8_q), .out(out_8), .sel(Reg_a_ser_lido_2));  // open: en
endmodule
