// Logisim project Flip-flop D OK.circ as structural Verilog: 2 circuits, main circuit CHIP Flip-flop D
module CHIP_Flip_flop_D (
  input  INPUT,
  input  Enable,
  input  Clear,
  output OUTPUT,
  output OUTPUT_BARRADO
);

  wire clock_1_out;

  Clock clock_1 (.out(clock_1_out));
  D_Flip_Flop d_ff_1 (
    .clk(clock_1_out), .D(INPUT), .Q(OUTPUT), .Qn(OUTPUT_BARRADO), .en(Enable), .reset(Clear));  // open: preset
endmodule

module Circuito_Flip_flop_D (
  input  INPUT,
  output OUTPUT,
  output OUTPUT_BARRADO
);

  wire CLOCK_out, nand_1_out, nand_2_out, not_1_out;

  Clock CLOCK (.out(CLOCK_out));
  not not_1 (not_1_out, INPUT);
  nand nand_1 (nand_1_out, INPUT, CLOCK_out);
  nand nand_2 (nand_2_out, CLOCK_out, not_1_out);
  nor nor_1 (OUTPUT, nand_1_out, OUTPUT_BARRADO);
  nor nor_2 (OUTPUT_BARRADO, OUTPUT, nand_2_out);
endmodule
