// Logisim project Flip-flop JK OK.circ as structural Verilog: 2 circuits, main circuit CHIP Flip-flop JK
module CHIP_Flip_flop_JK (
  input  J,
  input  K,
  input  Preset,
  input  Enable,
  input  Clear,
  output OUTPUT,
  output OUTPUT_BARRADO
);

  wire CLOCK_out;

  Clock CLOCK (.out(CLOCK_out));
  J_K_Flip_Flop j_k_ff_1 (
    .J(J), .clk(CLOCK_out), .K(K), .Q(OUTPUT), .Qn(OUTPUT_BARRADO), .preset(Preset), .en(Enable),
    .reset(Clear));
endmodule

module Circuito_Flip_flop_JK (
  input  J,
  input  K,
  output OUTPUT,
  output OUTPUT_BARRADO
);

  wire CLOCK_out, nand_1_out, nand_2_out;

  Clock CLOCK (.out(CLOCK_out));
  nand nand_1 (nand_1_out, OUTPUT_BARRADO, J, CLOCK_out);
  nand nand_2 (nand_2_out, CLOCK_out, K, OUTPUT);
  nand nand_3 (OUTPUT, nand_1_out, OUTPUT_BARRADO);
  nand nand_4 (OUTPUT_BARRADO, OUTPUT, nand_2_out);
endmodule
