// Logisim project Multiplexador de 4 entradas OK.circ as structural Verilog: 1 circuit, main circuit main
module main (
  input  A,
  input  B,
  input  C,
  input  D,
  input  SEL1,
  input  SEL_2,
  output out_7
);

  wire and_1_out, and_2_out, and_3_out, and_4_out, not_1_out, not_2_out;

  not not_1 (not_1_out, SEL1);
  not not_2 (not_2_out, SEL_2);
  and and_1 (and_1_out, A, SEL1, SEL_2);
  and and_2 (and_2_out, B, not_1_out, SEL_2);
  and and_3 (and_3_out, C, not_2_out, SEL1);
  and and_4 (and_4_out, D, not_1_out, not_2_out);
  or or_1 (out_7, and_1_out, and_2_out, and_3_out, and_4_out);

  // Notes on the sheet:
  //   SELETOR
  //   00
  //   10
  //   11
  //   SAÍDA
  //   D
  //   B
  //   01
  //   C
  //   A
endmodule
