// Logisim project RAM OK.circ as structural Verilog: 1 circuit, main circuit Memoria Ram
module Memoria_Ram (
  input  [7:0] dado_a_ser_escrito,
  input  [7:0] seletor,
  input  Enable_do_seletor,
  input  load,
  input  clear,
  input  [7:0] dado_a_ser_escrito_2,
  input  [1:0] \endereço ,
  input  load_read,
  input  Select,
  input  Clear_2,
  output [7:0] dado_lido,
  output [7:0] Dado_lido_2
);

  wire clock_2_out, clock_out, demultiplexer_2_out0, demultiplexer_2_out1, demultiplexer_2_out2,
       demultiplexer_2_out3, not_1_out, not_2_out;
  wire [1:0] controlled_buffer_2_out;
  wire [7:0] demultiplexer_1_out0, demultiplexer_1_out1, demultiplexer_1_out2, demultiplexer_1_out3,
       register_1_q, register_2_q, register_3_q, register_4_q;

  Clock clock (.out(clock_out));
  assign dado_lido = not_1_out ? dado_a_ser_escrito : 8'bz;  // Controlled_Buffer controlled_buffer_1
  not not_1 (not_1_out, load);
  RAM ram_1 (.addr(seletor), .data(dado_lido), .sel(Enable_do_seletor), .clk(clock_out), .ld(load), .clr(clear));
  not not_2 (not_2_out, load_read);
  assign controlled_buffer_2_out = Select ? \endereço  : 2'bz;  // Controlled_Buffer controlled_buffer_2
  Demultiplexer #(.select(2), .width(8)) demultiplexer_1 (
    .out0(demultiplexer_1_out0), .out1(demultiplexer_1_out1), .out2(demultiplexer_1_out2),
    .out3(demultiplexer_1_out3), .in(dado_a_ser_escrito_2), .sel(controlled_buffer_2_out), .en(not_2_out));
  Register register_1 (
    .D(demultiplexer_1_out0), .Q(register_1_q), .clk(demultiplexer_2_out0), .clr(Clear_2));  // open: en
  Demultiplexer #(.select(2)) demultiplexer_2 (
    .out0(demultiplexer_2_out0), .out1(demultiplexer_2_out1), .out2(demultiplexer_2_out2),
    .out3(demultiplexer_2_out3), .in(clock_2_out), .sel(controlled_buffer_2_out), .en(not_2_out));
  Clock clock_2 (.out(clock_2_out));
  Register register_2 (
    .D(demultiplexer_1_out2), .Q(register_2_q), .clk(demultiplexer_2_out2), .clr(Clear_2));  // open: en
  Register register_3 (
    .D(demultiplexer_1_out1), .Q(register_3_q), .clk(demultiplexer_2_out1), .clr(Clear_2));  // open: en
  Register register_4 (
    .D(demultiplexer_1_out3), .Q(register_4_q), .clk(demultiplexer_2_out3), .clr(Clear_2));  // open: en
  Multiplexer #(.select(2), .width(8)) multiplexer_1 (
    .in0(register_4_q), .in1(register_2_q), .in2(register_3_q), .in3(register_1_q), .out(Dado_lido_2),
    .sel(controlled_buffer_2_out), .en(load_read));
endmodule
