// Logisim project ROM OK.circ as structural Verilog: 1 circuit, main circuit Memoria Rom
module Memoria_Rom (
  input  [7:0] seletor,
  input  Enable_do_seletor,
  input  [1:0] \Endereço ,
  input  Enable_do_seletor_2,
  output [7:0] \output_da_memória ,
  output [7:0] Output
);

  wire Clock_out;
  wire [7:0] register_1_q, register_2_q, register_3_q, register_4_q;

  ROM rom_1 (.addr(seletor), .data(\output_da_memória ), .sel(Enable_do_seletor));
  Clock Clock (.out(Clock_out));
  Register register_1 (.D(8'h1), .Q(register_1_q), .clk(Clock_out));  // open: en, clr
  Register register_2 (.D(8'h10), .Q(register_2_q), .clk(Clock_out));  // open: en, clr
  Register register_3 (.D(8'h11), .Q(register_3_q), .clk(Clock_out));  // open: en, clr
  Register register_4 (.D({8{1'b0}}), .Q(register_4_q), .clk(Clock_out));  // open: en, clr
  Multiplexer #(.select(2), .width(8)) multiplexer_1 (
    .in0(register_4_q), .in1(register_3_q), .in2(register_2_q), .in3(register_1_q), .out(Output),
    .sel(\Endereço ), .en(Enable_do_seletor_2));

  // Notes on the sheet:
  //   contents of rom_1 (hex, n*v repeats v):
  //   3a 35 3b 35 53 66 3c 22 56 9d 66 13 54 22 52 53
endmodule
