// Logisim project Somador 8 bits e de 8 bits com 4 OK.circ as structural Verilog
module somador_1_bit (
  input  A,
  input  B,
  input  CARRY_IN,
  output SOMA,
  output CARRY_OUT
);

  wire and_1_out, and_2_out, and_3_out, xor_1_out;

  and and_1 (and_1_out, A, B);
  and and_2 (and_2_out, A, CARRY_IN);
  and and_3 (and_3_out, B, CARRY_IN);
  xor xor_1 (xor_1_out, A, B);
  xor xor_2 (SOMA, xor_1_out, CARRY_IN);
  or or_1 (CARRY_OUT, and_1_out, and_2_out, and_3_out);
endmodule

module somador_de_4_bits (
  input  C_IN,
  input  a3,
  input  a2,
  input  a1,
  input  a0,
  input  b3,
  input  b2,
  input  b1,
  input  b0,
  output CARRY_OUT_S,
  output s3,
  output s2,
  output s1,
  output s0
);

  wire somador_1_bit_2_carry_out, somador_1_bit_3_carry_out, somador_1_bit_4_carry_out;

  somador_1_bit somador_1_bit_1 (
    .A(b3), .B(a3), .CARRY_IN(somador_1_bit_2_carry_out), .SOMA(s3), .CARRY_OUT(CARRY_OUT_S));
  somador_1_bit somador_1_bit_2 (
    .A(b2), .B(a2), .CARRY_IN(somador_1_bit_3_carry_out), .SOMA(s2), .CARRY_OUT(somador_1_bit_2_carry_out));
  somador_1_bit somador_1_bit_3 (
    .A(b1), .B(a1), .CARRY_IN(somador_1_bit_4_carry_out), .SOMA(s1), .CARRY_OUT(somador_1_bit_3_carry_out));
  somador_1_bit somador_1_bit_4 (.A(b0), .B(a0), .CARRY_IN(C_IN), .SOMA(s0), .CARRY_OUT(somador_1_bit_4_carry_out));
endmodule

module Somador_8_bits (
  input  b7,
  input  b6,
  input  b5,
  input  b4,
  input  b3,
  input  b2,
  input  b1,
  input  b0,
  input  a7,
  input  a6,
  input  a5,
  input  a4,
  input  a3,
  input  a2,
  input  a1,
  input  a0,
  input  carry_in,
  output s7,
  output s6,
  output s5,
  output s4,
  output s3,
  output s2,
  output s1,
  output s0,
  output overflow
);

  wire somador_de_4_bits_2_carry_out_s;

  somador_de_4_bits somador_de_4_bits_1 (
    .CARRY_OUT_S(overflow), .C_IN(somador_de_4_bits_2_carry_out_s), .a3(a7), .a2(a6), .a1(a5), .a0(a4),
    .b3(b7), .b2(b6), .b1(b5), .b0(b4), .s3(s7), .s2(s6), .s1(s5), .s0(s4));
  somador_de_4_bits somador_de_4_bits_2 (
    .CARRY_OUT_S(somador_de_4_bits_2_carry_out_s), .C_IN(carry_in), .a3(a3), .a2(a2), .a1(a1), .a0(a0),
    .b3(b3), .b2(b2), .b1(b1), .b0(b0), .s3(s3), .s2(s2), .s1(s1), .s0(s0));
endmodule

module Somador_8_bits_com_4 (
  input  a7,
  input  a6,
  input  a5,
  input  a4,
  input  a3,
  input  a2,
  input  a1,
  input  a0,
  input  in_9,
  output s7,
  output s6,
  output s5,
  output s4,
  output s3,
  output s2,
  output s1,
  output s0,
  output overflow
);

  Somador_8_bits somador_8_bits_1 (
    .a7(a7), .a6(a6), .a5(a5), .a4(a4), .a3(a3), .a2(a2), .a1(a1), .a0(a0), .b7(1'b0), .b6(1'b0), .b5(1'b0),
    .b4(1'b0), .b3(1'b0), .b2(1'b1), .b1(1'b0), .b0(1'b0), .s7(s7), .s6(s6), .s5(s5), .s4(s4), .s3(s3),
    .s2(s2), .s1(s1), .s0(s0), .carry_in(in_9), .overflow(overflow));
endmodule
