// Logisim project ULA  de 8 bits OK.circ as structural Verilog: 1 circuit, main circuit main
module main (
  input  [7:0] A,
  input  [7:0] B,
  input  [2:0] Shift_de_3_bits,
  input  [3:0] Seletor,
  output [7:0] OUTPUT,
  output carry_overflow,
  output carry_overflow_2
);

  wire [7:0] adder_1_out, AND_out, NAND_out, NOR_out, not_1_out, OR_out, shifter_1_out, shifter_2_out,
       subtractor_1_out, XOR_out;

  assign AND_out = A & B;  // AND_Gate AND, 8 bits wide
  assign OR_out = A | B;  // OR_Gate OR, 8 bits wide
  assign not_1_out = ~A;  // NOT_Gate not_1, 8 bits wide
  assign NOR_out = ~(A | B);  // NOR_Gate NOR, 8 bits wide
  assign NAND_out = ~(A & B);  // NAND_Gate NAND, 8 bits wide
  assign XOR_out = A ^ B;  // XOR_Gate XOR, 8 bits wide
  Shifter shifter_1 (.in(A), .\dist (Shift_de_3_bits), .out(shifter_1_out));
  Shifter #(.shift("ar")) shifter_2 (.in(A), .\dist (Shift_de_3_bits), .out(shifter_2_out));
  Adder adder_1 (.a(A), .b(B), .out(adder_1_out), .cout(carry_overflow));  // open: cin
  Subtractor subtractor_1 (.a(A), .b(B), .out(subtractor_1_out), .bout(carry_overflow_2));  // open: bin
  Multiplexer #(.select(4), .width(8)) multiplexer_1 (
    .in0(AND_out), .in1(OR_out), .in2(not_1_out), .in3(NOR_out), .in4(NAND_out), .in5(XOR_out),
    .in6(shifter_1_out), .in7(shifter_2_out), .in8(adder_1_out), .in9(subtractor_1_out), .out(OUTPUT),
    .sel(Seletor));  // open: in10, in11, in12, in13, in14, in15, en

  // Notes on the sheet:
  //   NOT
  //   SOMADOR
  //   SUBTRADOR
  //   SHIFT A ESQUERDA
  //   SHIFT A DIREITA
  //   Código seletor
  //   0000 porta AND
  //   0001 porta OR
  //   0011 porta NOR
  //   0100 porta NAND
  //   0101 porta XOR
  //   1000 SOMADO
  //   0010 porta NOT A
  //   0110 Shift 3 bits a esquerda
  //   0111 Shift 3 bits a direita
  //   1001 SUBTRADOR
endmodule
