// Logisim project Unidade de Controle OK.circ as structural Verilog: 1 circuit, main circuit main
module main (
  input  [2:0] _110_SLTI,
  output Branch,
  output Jump,
  output ALUSrc,
  output ALUOP,
  output MemRead,
  output MemWrite,
  output RegWrite,
  output RegDst,
  output MemtoReg
);

  Multiplexer #(.select(3), .width(9), .disabled(0)) multiplexer_1 (
    .in0(9'h26), .in1(9'h79), .in2(9'h64), .in3(9'h120), .in4(9'h80), .in5(9'h87), .in6(9'h64),
    .out({Branch, Jump, ALUSrc, ALUOP, MemRead, MemWrite, RegWrite, RegDst, MemtoReg}), .sel(_110_SLTI));  // open: in7, en

  // Notes on the sheet:
  //   000 TIPO-R
  //   001 LOAD
  //   010 STORE
  //   011 BEQ
  //   100 JUMP
  //   101 JAL
endmodule
